# Fritzing sketch TFM_Sketch2 (saved by Fritzing 0.9.3b)
breadboards: 1

parts:
  Componente1 = Arduino Mega 2560 (Rev3)
  Componente4 = FC-28 Soil Hygrometer Module
  Componente3 = FC-28 Soil Hygrometer Module
  Componente5 = FC-28 Soil Hygrometer Module
  Componente2 = FC-28 Soil Hygrometer Module

nets:
  N1: Componente1.A0, Componente2.AO
  N2: Componente1.A2, Componente4.AO
  N3: Componente1.A3, Componente5.AO
  VCC: Componente1.5V, Componente4.VCC, Componente3.VCC, Componente5.VCC, Componente2.VCC
  GND: Componente1.GND, Componente4.GND, Componente3.GND, Componente5.GND, Componente2.GND

custom parts:
  FC-28 Soil Hygrometer Module: The FC-28 is a soil hygrometer module that uses the Texas Instruments LM393 comparator chip to provide an analog measurement of soil humidity. The digital output is high when soil moisture is over a certain threshold, as determined by adjusting the potentiometer.
